// Digital circuit VGA Monitor.dig as structural Verilog
module VGA_Monitor (
  input  clk
);

  wire and_1_out, and_2_out, and_3_out, comparator_1_gt, comparator_2_lt, comparator_3_gt, comparator_4_lt,
       multiplexer_1_out, rst_out, vgatiming_1_hsync, vgatiming_1_videoactive, vgatiming_1_vsync;
  wire [9:0] keyboradcontrol_1_down, keyboradcontrol_1_left, keyboradcontrol_1_right, keyboradcontrol_1_up,
       vgatiming_1_x, vgatiming_1_y;

  Button rst (.out(rst_out));
  keyBoradControl keyboradcontrol_1 (
    .clk(clk), .rst(rst_out), .left(keyboradcontrol_1_left), .right(keyboradcontrol_1_right),
    .up(keyboradcontrol_1_up), .down(keyboradcontrol_1_down));
  vgaTiming vgatiming_1 (
    .clk(clk), .X(vgatiming_1_x), .Y(vgatiming_1_y), .Hsync(vgatiming_1_hsync), .Vsync(vgatiming_1_vsync),
    .VideoActive(vgatiming_1_videoactive));
  Comparator #(.Bits(10)) comparator_1 (
    .a(vgatiming_1_x), .b(keyboradcontrol_1_left), .gt(comparator_1_gt));  // open: eq, lt
  Comparator #(.Bits(10)) comparator_2 (
    .a(vgatiming_1_x), .b(keyboradcontrol_1_right), .lt(comparator_2_lt));  // open: gt, eq
  Comparator #(.Bits(10)) comparator_3 (
    .a(vgatiming_1_y), .b(keyboradcontrol_1_up), .gt(comparator_3_gt));  // open: eq, lt
  Comparator #(.Bits(10)) comparator_4 (
    .a(vgatiming_1_y), .b(keyboradcontrol_1_down), .lt(comparator_4_lt));  // open: gt, eq
  and and_1 (and_1_out, comparator_1_gt, comparator_2_lt);
  and and_2 (and_2_out, comparator_3_gt, comparator_4_lt);
  and and_3 (and_3_out, and_1_out, and_2_out);
  Multiplexer multiplexer_1 (.sel(vgatiming_1_videoactive), .in_0(1'b0), .in_1(and_3_out), .out(multiplexer_1_out));
  VGA vga_1 (.R(multiplexer_1_out), .G(1'b0), .B(1'b0), .H(vgatiming_1_hsync), .V(vgatiming_1_vsync), .C(clk));

  // Notes on the sheet:
  //   clk: Hz: 2147483647
endmodule
