// Digital circuit keyBoradControl.dig as structural Verilog
module keyBoradControl (
  input  clk,
  input  rst,
  output [9:0] left,
  output [9:0] right,
  output [9:0] up,
  output [9:0] down
);

  wire comparator_1_eq, comparator_2_eq, comparator_3_eq, comparator_4_eq, or_1_out, or_2_out;
  wire [9:0] keyboard_1_d;
  wire [15:10] keyboard_1_d_2;

  Keyboard keyboard_1 (.C(clk), .en(1'b1), .D({keyboard_1_d_2, keyboard_1_d}));  // open: av
  Comparator #(.Bits(10)) comparator_1 (.a(keyboard_1_d), .b(10'h41), .eq(comparator_1_eq));  // open: gt, lt
  Comparator #(.Bits(10)) comparator_2 (.a(keyboard_1_d), .b(10'h44), .eq(comparator_2_eq));  // open: gt, lt
  Comparator #(.Bits(10)) comparator_3 (.a(keyboard_1_d), .b(10'h57), .eq(comparator_3_eq));  // open: gt, lt
  Comparator #(.Bits(10)) comparator_4 (.a(keyboard_1_d), .b(10'h53), .eq(comparator_4_eq));  // open: gt, lt
  or or_1 (or_1_out, comparator_2_eq, comparator_1_eq);
  or or_2 (or_2_out, comparator_4_eq, comparator_3_eq);
  CounterPreset #(.Bits(10), .isProgramCounter("true")) u_LEFT (
    .en(or_1_out), .C(clk), .dir(comparator_1_eq), .in(10'h13f), .ld(rst), .clr(1'b0), .out(left));  // open: ovf
  CounterPreset #(.Bits(10)) u_RIGHT (
    .en(or_1_out), .C(clk), .dir(comparator_1_eq), .in(10'h161), .ld(rst), .clr(1'b0), .out(right));  // open: ovf
  CounterPreset #(.Bits(10), .isProgramCounter("true")) u_UP (
    .en(or_2_out), .C(clk), .dir(comparator_3_eq), .in(10'hef), .ld(rst), .clr(1'b0), .out(up));  // open: ovf
  CounterPreset #(.Bits(10)) u_DOWN (
    .en(or_2_out), .C(clk), .dir(comparator_3_eq), .in(10'h10f), .ld(rst), .clr(1'b0), .out(down));  // open: ovf

  // Notes on the sheet:
  //   clk: Hz: 5
endmodule
