// Digital circuit vgaTiming.dig as structural Verilog
module vgaTiming (
  input  clk,
  output [9:0] X,
  output [9:0] Y,
  output Hsync,
  output Vsync,
  output VideoActive
);

  wire and_1_out, and_2_out, comparator_3_eq, comparator_3_gt, comparator_4_lt, comparator_5_eq,
       comparator_5_gt, comparator_6_lt, comparator_7_lt, comparator_8_lt, h_rst, or_1_out, or_2_out, v_rst;
  wire [9:0] h_count, sub_1_s, sub_2_s, v_count;

  Counter #(.Bits(10)) Horizontal (.en(1'b1), .C(clk), .clr(h_rst), .out(h_count));  // open: ovf
  Sub #(.Bits(10)) sub_1 (.a(10'h320), .b(10'h1), .c_i(1'b0), .s(sub_1_s));  // open: c_o
  Sub #(.Bits(10)) sub_2 (.a(10'h20d), .b({10{1'b0}}), .c_i(1'b0), .s(sub_2_s));  // open: c_o
  Comparator #(.Bits(10)) comparator_1 (.a(h_count), .b(sub_1_s), .eq(h_rst));  // open: gt, lt
  Comparator #(.Bits(10)) comparator_2 (.a(v_count), .b(sub_2_s), .eq(v_rst));  // open: gt, lt
  Counter #(.Bits(10)) Vertical (.en(h_rst), .C(clk), .clr(v_rst), .out(v_count));  // open: ovf
  Comparator #(.Bits(10)) comparator_3 (
    .a(h_count), .b(10'h290), .gt(comparator_3_gt), .eq(comparator_3_eq));  // open: lt
  Comparator #(.Bits(10)) comparator_4 (.a(h_count), .b(10'h2f0), .lt(comparator_4_lt));  // open: gt, eq
  Comparator #(.Bits(10)) comparator_5 (
    .a(v_count), .b(10'h1ea), .gt(comparator_5_gt), .eq(comparator_5_eq));  // open: lt
  Comparator #(.Bits(10)) comparator_6 (.a(v_count), .b(10'h1ec), .lt(comparator_6_lt));  // open: gt, eq
  Comparator #(.Bits(10)) comparator_7 (.a(h_count), .b(10'h280), .lt(comparator_7_lt));  // open: gt, eq
  Comparator #(.Bits(10)) comparator_8 (.a(v_count), .b(10'h1e0), .lt(comparator_8_lt));  // open: gt, eq
  or or_1 (or_1_out, comparator_3_gt, comparator_3_eq);
  or or_2 (or_2_out, comparator_5_gt, comparator_5_eq);
  and and_1 (and_1_out, or_1_out, comparator_4_lt);
  and and_2 (and_2_out, or_2_out, comparator_6_lt);
  Multiplexer #(.Bits(10)) multiplexer_1 (.sel(comparator_7_lt), .in_0({10{1'b0}}), .in_1(h_count), .out(X));
  Multiplexer #(.Bits(10)) multiplexer_2 (.sel(comparator_8_lt), .in_0({10{1'b0}}), .in_1(v_count), .out(Y));
  Multiplexer multiplexer_3 (.sel(and_1_out), .in_0(1'b1), .in_1(1'b0), .out(Hsync));
  Multiplexer multiplexer_4 (.sel(and_2_out), .in_0(1'b1), .in_1(1'b0), .out(Vsync));
  // Probe on X
  and and_3 (VideoActive, comparator_7_lt, comparator_8_lt);

  // Notes on the sheet:
  //   clk: Hz: 10
endmodule
